# Fritzing sketch sensor (saved by Fritzing 0.9.3b)
breadboards: 1

parts:
  R2 = Resistor [tolerance=±5% resistance=10k package="1206 [SMD]"]
  R1 = Resistor [tolerance=±5% resistance=100 package="1206 [SMD]"]
  Part1 = KY-005 Infrared Transmitter Module [package="Breakout board"]
  5v_usb = Power plug
  Composant1 = Arduino Nano (Rev3.0)
  Part2 = KY-022 Infrared Receiver Module [package="Breakout board"]
  NRF24L1 = NRF24L01 SMD [package="SO8 [SMD]"]

nets:
  VIN: R2.Pin_0, Part1.Vin, 5v_usb.VCC, Part2.Vin
  N1: R2.Pin_1, Part2.S
  N2: R1.Pin_0, Composant1.D6
  N3: R1.Pin_1, Part1.S
  GND: Part1.-, 5v_usb.GND, Composant1.GND, Part2.-, NRF24L1.GND
  N4: Composant1.D9, NRF24L1.CE
  N5: Composant1.D10, NRF24L1.CSN
  N6: Composant1.D11/MOSI, NRF24L1.MOSI
  N7: Composant1.D12/MISO, NRF24L1.MISO
  3V3: Composant1.3V3, NRF24L1.VCC
  N8: Composant1.D13/SCK, NRF24L1.SCK

custom parts:
  KY-005 Infrared Transmitter Module: Arduino IR Transmitter Module Keyes KY-005, emits infrared light at 38KHz.
  KY-022 Infrared Receiver Module: Arduino IR receiver module KY-022, reacts to 38kHz infrared light.
